# Fritzing sketch ic74HC163 (saved by Fritzing 0.9.3b)
breadboards: 1

parts:
  IC1 = SHIFT REGISTER [package=dil16]
  Part1 = Arduino Uno (Rev3)
  LED1 = smd LED [color="Red (633nm)" package="0603 [SMD]"]
  LED2 = smd LED [color="Red (633nm)" package="0603 [SMD]"]
  LED3 = smd LED [color="Red (633nm)" package="0603 [SMD]"]
  LED4 = smd LED [color="Red (633nm)" package="0603 [SMD]"]
  R1 = Resistor [tolerance=±5% resistance=220 package="2512 [SMD]"]
  R2 = Resistor [tolerance=±5% resistance=220 package="2512 [SMD]"]
  R3 = Resistor [tolerance=±5% resistance=220 package="2512 [SMD]"]
  R4 = Resistor [tolerance=±5% resistance=220 package="2512 [SMD]"]
  S1 = Pushbutton [package="[THT]"]
  R5 = Resistor [tolerance=±5% resistance=10k package="2512 [SMD]"]

nets:
  N1: IC1.QC, Part1.D13/SCK
  N2: IC1.QD, Part1.D12/MISO
  GND: IC1.GND, Part1.GND, R1.Pin_0, R2.Pin_0, R3.Pin_0, R4.Pin_0, R5.Pin_0
  N3: IC1.SCK, LED4.anode
  N4: IC1.RCK, LED3.anode
  N5: IC1.G, LED2.anode
  N6: IC1.SER, LED1.anode
  VCC: IC1.VCC, Part1.5V, S1.Pin_3, S1.Pin_4
  N7: Part1.D2, S1.Pin_1, S1.Pin_2, R5.Pin_1
  N8: LED1.cathode, R3.Pin_1
  N9: LED2.cathode, R1.Pin_1
  N10: LED3.cathode, R2.Pin_1
  N11: LED4.cathode, R4.Pin_1
