# Fritzing sketch 74HC595 (saved by Fritzing 0.9.3b)
breadboards: 1

parts:
  Part1 = Arduino Uno (Rev3)
  U1 = 74HC595 [package="DIP16 [THT]"]
  LED1 = smd LED [color="Red (633nm)" package="0603 [SMD]"]
  LED2 = smd LED [color="Red (633nm)" package="0603 [SMD]"]
  LED3 = smd LED [color="Red (633nm)" package="0603 [SMD]"]
  LED4 = smd LED [color="Red (633nm)" package="0603 [SMD]"]
  LED5 = smd LED [color="Red (633nm)" package="0603 [SMD]"]
  LED6 = smd LED [color="Red (633nm)" package="0603 [SMD]"]
  LED7 = smd LED [color="Red (633nm)" package="0603 [SMD]"]
  LED8 = smd LED [color="Red (633nm)" package="0603 [SMD]"]
  R1 = Resistor [tolerance=±5% resistance=220 package="0603 [SMD]"]
  R2 = Resistor [tolerance=±5% resistance=220 package="0603 [SMD]"]
  R3 = Resistor [tolerance=±5% resistance=220 package="0603 [SMD]"]
  R4 = Resistor [tolerance=±5% resistance=220 package="0603 [SMD]"]
  R5 = Resistor [tolerance=±5% resistance=220 package="0603 [SMD]"]
  R6 = Resistor [tolerance=±5% resistance=220 package="0603 [SMD]"]
  R8 = Resistor [tolerance=±5% resistance=220 package="0603 [SMD]"]
  R9 = Resistor [tolerance=±5% resistance=220 package="0603 [SMD]"]

nets:
  N1: Part1.D10_PWM/SS, U1.ST_CP
  N2: Part1.D11_PWM/MOSI, U1.SH_CP
  N3: Part1.D12/MISO, U1.DS
  5V: Part1.5V, U1.MR, U1.VCC
  GND: Part1.GND, U1.GND, U1.OE, R1.Pin_1, R2.Pin_1, R3.Pin_1, R4.Pin_1, R5.Pin_1, R6.Pin_1, R9.Pin_1
  N4: U1.Q1, LED2.cathode
  N5: U1.Q2, LED3.cathode
  N6: U1.Q3, LED4.cathode
  N7: U1.Q4, LED5.cathode
  N8: U1.Q5, LED6.cathode
  N9: U1.Q6, LED7.cathode
  N10: U1.Q7, LED8.cathode
  N11: U1.Q0, LED1.cathode
  N12: LED1.anode, R1.Pin_0
  N13: LED2.anode, R2.Pin_0
  N14: LED3.anode, R4.Pin_0
  N15: LED4.anode, R3.Pin_0
  N16: LED5.anode, R5.Pin_0
  N17: LED6.anode, R9.Pin_0
  N18: LED7.anode, R6.Pin_0
  N19: LED8.anode, R8.Pin_0
