# Fritzing sketch simpleSeq4 (saved by Fritzing 0.9.3b)
circuit board: 8.46667cm x 5.64444cm
breadboards: 1

parts:
  Teensy_3_1 = Teensy 3.1
  S2 = Pushbutton [package="[THT]"]
  R2 = Resistor [tolerance=±5% resistance=10k package=THT]
  S3 = Pushbutton [package="[THT]"]
  R3 = Resistor [tolerance=±5% resistance=10k package=THT]
  S4 = Pushbutton [package="[THT]"]
  R4 = Resistor [tolerance=±5% resistance=10k package=THT]
  S5 = Pushbutton [package="[THT]"]
  R5 = Resistor [tolerance=±5% resistance=10k package=THT]
  R6 = Resistor [tolerance=±5% resistance=220 package="0402 [SMD]"]
  R7 = Resistor [tolerance=±5% resistance=220 package="0402 [SMD]"]
  R8 = Resistor [tolerance=±5% resistance=220 package="0402 [SMD]"]
  R9 = Resistor [tolerance=±5% resistance=220 package="0402 [SMD]"]
  LED1 = smd LED [color="Red (633nm)" package="0603 [SMD]"]
  LED2 = smd LED [color="Red (633nm)" package="0603 [SMD]"]
  LED3 = smd LED [color="Red (633nm)" package="0603 [SMD]"]
  LED4 = smd LED [color="Red (633nm)" package="0603 [SMD]"]
  U1 = 2.5mm Audio Jack [package=stereojack2.5mm_specia_pogopins]
  U2 = 2.5mm Audio Jack [package=stereojack2.5mm_specia_pogopins]
  R10 = Resistor [tolerance=±5% resistance=220 package=THT]

nets:
  N1: Teensy_3_1.D8, U1.SLEEVE
  N2: Teensy_3_1.D13, S2.Pin_1, S2.Pin_2, R2.Pin_1
  N3: Teensy_3_1.A0/D14, S3.Pin_1, S3.Pin_2, R3.Pin_1
  N4: Teensy_3_1.A1/D15, S4.Pin_1, S4.Pin_2, R4.Pin_1
  N5: Teensy_3_1.A2/D16, S5.Pin_1, S5.Pin_2, R5.Pin_1
  N6: Teensy_3_1.A6/D20, LED1.anode
  N7: Teensy_3_1.A7/D21, LED2.anode
  N8: Teensy_3_1.A8/D22, LED3.anode
  N9: Teensy_3_1.A9/D23, LED4.anode
  N10: S2.Pin_3, S2.Pin_4, S3.Pin_3, S3.Pin_4, S4.Pin_3, S4.Pin_4, S5.Pin_3, S5.Pin_4
  N11: R2.Pin_0, R3.Pin_0, R4.Pin_0, R5.Pin_0, R6.Pin_1, R7.Pin_1, R8.Pin_1, R9.Pin_1, U1.LEFT, U2.LEFT
  N12: R6.Pin_0, LED1.cathode
  N13: R7.Pin_0, LED2.cathode
  N14: R8.Pin_0, LED3.cathode
  N15: R9.Pin_0, LED4.cathode
  N16: U2.SLEEVE, R10.Pin_0

notes:
  Clock Input
  (mono)
  tip = hot
  Trigger Output
  Schematics not maintained.
