# Fritzing sketch digitalRandomizer (saved by Fritzing 0.9.3b)
breadboards: 1

parts:
  Teensy1 = Teensy 3.0
  R1 = Rotary Potentiometer (Small) [maximum_resistance=10kΩ package=THT]
  R2 = Rotary Potentiometer (Small) [maximum_resistance=10kΩ package=THT]
  U1 = 3.5mm Audio Jack [package=audio-jack-3.5mm-smd]
  U3 = 3.5mm Audio Jack [package=audio-jack-3.5mm-smd]
  U2 = 3.5mm Audio Jack [package=audio-jack-3.5mm-smd]

nets:
  N1: Teensy1.D10, U2.LEFT
  N2: Teensy1.D11, U3.LEFT
  N3: Teensy1.D12, U1.LEFT
  N4: Teensy1.A0/D14, R1.wiper
  N5: Teensy1.A1/D15, R2.wiper
  N6: R1.leg1, R2.leg1, U1.SLEEVE, U3.SLEEVE, U2.SLEEVE
  N7: R1.leg2, R2.leg2
