# Fritzing sketch digitalRandomizer (saved by Fritzing 0.9.3b)
breadboards: 1

parts:
  R1 = Rotary Potentiometer (Small) [maximum_resistance=10kΩ package=THT]
  R2 = Rotary Potentiometer (Small) [maximum_resistance=10kΩ package=THT]
  U1 = 3.5mm Audio Jack [package=audio-jack-3.5mm-smd]
  U3 = 3.5mm Audio Jack [package=audio-jack-3.5mm-smd]
  U2 = 3.5mm Audio Jack [package=audio-jack-3.5mm-smd]
  Teensy1 = Teensy 3.1

nets:
  N1: R1.leg1, R2.leg1, U1.SLEEVE, U3.SLEEVE, U2.SLEEVE
  N2: R1.wiper, Teensy1.A0/D14
  N3: R1.leg2, R2.leg2
  N4: R2.wiper, Teensy1.A1/D15
  N5: U1.LEFT, Teensy1.D12
  N6: U3.LEFT, Teensy1.D11
  N7: U2.LEFT, Teensy1.D10
